# Fritzing sketch schema complet (saved by Fritzing 0.9.3b)
breadboards: 1

parts:
  Composant1 = Arduino Nano (Rev3.0) (ICSP)
  ZS-042_RTC1 = ZS-042 RTC Module  # not connected
  Squix1 = OLED 0.96" 128x64 I2C SSD1306
  LED1 = smd LED [color="Red (633nm)" package="0805 [SMD]"]
  R1 = Resistor [tolerance=±5% resistance=1k package="0402 [SMD]"]
  AD1 = DDS AD9850
  BS170 = MOSFET-NCHANNEL [package=to-92]
  VK200 = Inductor [package="0603 [SMD]"]
  C1 = Electrolytic Capacitor [capacitance=100μF package="0807 [SMD, electrolytic]"]
  100uh = Inductor [package="0603 [SMD]"]
  U1 = BNC [package=bnc]
  1_5uH = Inductor [package="0603 [SMD]"]
  C2 = Ceramic Capacitor [capacitance=100nF package="200 mil [THT, multilayer]"]
  1_5uH_2 = Inductor [package="0603 [SMD]"]
  C3 = Ceramic Capacitor [capacitance=100nF package="200 mil [THT, multilayer]"]
  C4 = Ceramic Capacitor [capacitance=390n package="200 mil [THT, multilayer]"]
  C5 = Ceramic Capacitor [capacitance=100nF package="200 mil [THT, multilayer]"]

nets:
  GND: Composant1.GND, Squix1.GND, LED1.cathode, AD1.GND, BS170.G, C1.-, U1.GND, C2.0, C3.0, C4.0
  N1: Composant1.D2, R1.Pin_0
  N2: Composant1.D9, AD1.RST
  N3: Composant1.D10, AD1.FQ
  N4: Composant1.D11/MOSI, AD1.DATA
  VCC: Composant1.5V, Squix1.VCC, AD1.VCC, VK200.pin_0
  N5: Composant1.A5, Squix1.SCL
  N6: Composant1.A4, Squix1.SCA
  N7: Composant1.D13/SCK, AD1.CLK
  N8: LED1.anode, R1.Pin_1
  N9: AD1.QN, BS170.S
  N10: BS170.D, 100uh.pin_1, C5.0
  N11: VK200.pin_1, C1.+, 100uh.pin_0
  N12: U1.OUT, C2.1, 1_5uH_2.pin_1
  N13: 1_5uH.pin_0, 1_5uH_2.pin_0, C3.1
  N14: 1_5uH.pin_1, C4.1, C5.1

notes:
  WSPR sur breadboard
  F4GOH 2019

custom parts:
  DDS AD9850: AD9850 DDS Signal Generator Module, frequency range 0 to 40MHz, sine or square wave output, on board 70MHz low pass filter, and 125MHz clock module. https://code.google.com/p/ad9850-arduino/
